// Logisim project DecodeIR.circ as structural Verilog: 1 circuit, main circuit DecodeIR
module DecodeIR (
  input  [31:0] IR,
  output WriteReg,
  output Store,
  output Load,
  output IN_OUT,
  output CTRL,
  output [2:0] GetOp,
  output [15:0] JMPAddress
);

  wire comparator_1_gt, comparator_2_eq, decoder_1_out1, or_1_out;
  wire [15:0] multiplexer_1_out;

  Comparator #(.width(3)) comparator_1 (.a(IR[4:2]), .b(3'b101), .gt(comparator_1_gt));  // open: eq, lt
  Comparator #(.width(3)) comparator_2 (.a(IR[4:2]), .b(3'b000), .eq(comparator_2_eq));  // open: gt, lt
  Decoder #(.select(2), .enable("false")) decoder_1 (
    .out0(WriteReg), .out1(decoder_1_out1), .out2(IN_OUT), .out3(CTRL), .sel(IR[1:0]));
  or or_1 (or_1_out, comparator_2_eq, comparator_1_gt);
  Multiplexer #(.width(16), .enable("false")) multiplexer_1 (
    .in0(IR[20:5]), .in1(IR[27:12]), .out(multiplexer_1_out), .sel(or_1_out));
  assign JMPAddress = CTRL ? multiplexer_1_out : 16'bz;  // Controlled_Buffer controlled_buffer_1
  Demultiplexer #(.enable("false")) demultiplexer_1 (.out0(Store), .out1(Load), .in(decoder_1_out1), .sel(IR[4]));

  assign GetOp = IR[4:2];
endmodule
