// Logisim project GetAddr.circ as structural Verilog: 1 circuit, main circuit main
module GetAddr (
  input  [15:0] PC,
  input  Load,
  input  Store,
  input  Fetch,
  output [15:0] Addr
);
endmodule
