// Logisim project Registres.circ as structural Verilog: 2 circuits, main circuit Registres
module Registres (
  input  [15:0] IN,
  input  [2:0] SR1,
  input  [2:0] SR2,
  input  [2:0] DR,
  input  WriteReg,
  input  Clock,
  input  Reset,
  output [15:0] R0,
  output [15:0] OUT_SR1,
  output [15:0] R1,
  output [15:0] R2,
  output [15:0] R3,
  output [15:0] OUT_SR2,
  output [15:0] R4,
  output [15:0] R5,
  output [15:0] OUT_DR,
  output [15:0] R6,
  output [15:0] R7
);

  wire demultiplexer_1_out0, demultiplexer_1_out1, demultiplexer_1_out2, demultiplexer_1_out3,
       demultiplexer_1_out4, demultiplexer_1_out5, demultiplexer_1_out6, demultiplexer_1_out7;
  wire [15:0] n16_bit_transistor_1_arith, n16_bit_transistor_2_arith, n16_bit_transistor_3_arith,
       n16_bit_transistor_4_arith, n16_bit_transistor_5_arith, n16_bit_transistor_6_arith,
       n16_bit_transistor_7_arith, n16_bit_transistor_8_arith;

  Demultiplexer #(.select(3)) demultiplexer_1 (
    .out0(demultiplexer_1_out0), .out1(demultiplexer_1_out1), .out2(demultiplexer_1_out2),
    .out3(demultiplexer_1_out3), .out4(demultiplexer_1_out4), .out5(demultiplexer_1_out5),
    .out6(demultiplexer_1_out6), .out7(demultiplexer_1_out7), .in(Clock), .sel(DR), .en(WriteReg));
  _16_bit_transistor u_16_bit_transistor_1 (.Test(demultiplexer_1_out0), .in_1(IN), .Arith(n16_bit_transistor_1_arith));
  _16_bit_transistor u_16_bit_transistor_2 (.Test(demultiplexer_1_out1), .in_1(IN), .Arith(n16_bit_transistor_2_arith));
  _16_bit_transistor u_16_bit_transistor_3 (.Test(demultiplexer_1_out2), .in_1(IN), .Arith(n16_bit_transistor_3_arith));
  _16_bit_transistor u_16_bit_transistor_4 (.Test(demultiplexer_1_out3), .in_1(IN), .Arith(n16_bit_transistor_4_arith));
  _16_bit_transistor u_16_bit_transistor_5 (.Test(demultiplexer_1_out4), .in_1(IN), .Arith(n16_bit_transistor_5_arith));
  _16_bit_transistor u_16_bit_transistor_6 (.Test(demultiplexer_1_out5), .in_1(IN), .Arith(n16_bit_transistor_6_arith));
  _16_bit_transistor u_16_bit_transistor_7 (.Test(demultiplexer_1_out6), .in_1(IN), .Arith(n16_bit_transistor_7_arith));
  _16_bit_transistor u_16_bit_transistor_8 (.Test(demultiplexer_1_out7), .in_1(IN), .Arith(n16_bit_transistor_8_arith));
  Register #(.width(16), .trigger("falling")) u_R0 (
    .D(n16_bit_transistor_1_arith), .Q(R0), .clk(Clock), .clr(Reset));  // open: en
  Register #(.width(16), .trigger("falling")) u_R1 (
    .D(n16_bit_transistor_2_arith), .Q(R1), .clk(Clock), .clr(Reset));  // open: en
  Register #(.width(16), .trigger("falling")) u_R2 (
    .D(n16_bit_transistor_3_arith), .Q(R2), .clk(Clock), .clr(Reset));  // open: en
  Register #(.width(16), .trigger("falling")) u_R3 (
    .D(n16_bit_transistor_4_arith), .Q(R3), .clk(Clock), .clr(Reset));  // open: en
  Register #(.width(16), .trigger("falling")) u_R4 (
    .D(n16_bit_transistor_5_arith), .Q(R4), .clk(Clock), .clr(Reset));  // open: en
  Register #(.width(16), .trigger("falling")) u_R5 (
    .D(n16_bit_transistor_6_arith), .Q(R5), .clk(Clock), .clr(Reset));  // open: en
  Register #(.width(16), .trigger("falling")) u_R6 (
    .D(n16_bit_transistor_7_arith), .Q(R6), .clk(Clock), .clr(Reset));  // open: en
  Register #(.width(16), .trigger("falling")) u_R7 (
    .D(n16_bit_transistor_8_arith), .Q(R7), .clk(Clock), .clr(Reset));  // open: en
  Multiplexer #(.select(3), .width(16)) multiplexer_1 (
    .in0(R0), .in1(R1), .in2(R2), .in3(R3), .in4(R4), .in5(R5), .in6(R6), .in7(R7), .out(OUT_SR1), .sel(SR1));  // open: en
  Multiplexer #(.select(3), .width(16)) multiplexer_2 (
    .out(OUT_SR2), .sel(SR2));  // open: in0, in1, in2, in3, in4, in5, in6, in7, en
  Multiplexer #(.select(3), .width(16)) multiplexer_3 (
    .out(OUT_DR), .sel(DR));  // open: in0, in1, in2, in3, in4, in5, in6, in7, en
endmodule

module _16_bit_transistor (
  input  [15:0] in_1,
  input  Test,
  output [15:0] Arith
);

  and and_1 (Arith[0], in_1[0], Test);
  and and_2 (Arith[1], in_1[1], Test);
  and and_3 (Arith[2], in_1[2], Test);
  and and_4 (Arith[3], in_1[3], Test);
  and and_5 (Arith[4], in_1[4], Test);
  and and_6 (Arith[5], in_1[5], Test);
  and and_7 (Arith[6], in_1[6], Test);
  and and_8 (Arith[7], in_1[7], Test);
  and and_9 (Arith[8], in_1[8], Test);
  and and_10 (Arith[9], in_1[9], Test);
  and and_11 (Arith[10], in_1[10], Test);
  and and_12 (Arith[11], in_1[11], Test);
  and and_13 (Arith[12], in_1[12], Test);
  and and_14 (Arith[13], in_1[13], Test);
  and and_15 (Arith[14], in_1[14], Test);
  and and_16 (Arith[15], in_1[15], Test);
endmodule
