// Logisim project Total.circ as structural Verilog: 11 circuits, main circuit main
module ALU (
  input  [15:0] Input1,
  input  [15:0] Input2,
  input  [15:0] Cst,
  input  Imm,
  input  [2:0] \Opération ,
  output Jump,
  output [15:0] Output,
  output Call,
  output Return
);

  wire and_2_out, comparator_1_eq, comparator_1_gt, comparator_1_lt, not_1_out, or_2_out;
  wire [15:0] adder_1_out, and_1_out, multiplexer_1_out, multiplier_1_out, or_1_out, shifter_1_out,
       shifter_2_out, subtractor_1_out, xor_1_out;

  Multiplexer #(.width(16), .enable("false")) multiplexer_1 (
    .in0(Input2), .in1(Cst), .out(multiplexer_1_out), .sel(Imm));
  Adder #(.width(16)) adder_1 (.a(Input1), .b(multiplexer_1_out), .out(adder_1_out));  // open: cin, cout
  Subtractor #(.width(16)) subtractor_1 (.a(Input1), .b(multiplexer_1_out), .out(subtractor_1_out));  // open: bin, bout
  assign and_1_out = Input1 & multiplexer_1_out;  // AND_Gate and_1, 16 bits wide
  assign or_1_out = Input1 | multiplexer_1_out;  // OR_Gate or_1, 16 bits wide
  assign xor_1_out = Input1 ^ multiplexer_1_out;  // XOR_Gate xor_1, 16 bits wide
  Shifter #(.width(16)) shifter_1 (.in(Input1), .\dist (multiplexer_1_out[15:12]), .out(shifter_1_out));
  Shifter #(.width(16), .shift("lr")) shifter_2 (.in(Input1), .\dist (multiplexer_1_out[15:12]), .out(shifter_2_out));
  Multiplier #(.width(16)) multiplier_1 (.a(Input1), .b(multiplexer_1_out), .out(multiplier_1_out));  // open: cin, cout
  Multiplexer #(.select(3), .width(16), .enable("false")) multiplexer_2 (
    .in0(adder_1_out), .in1(subtractor_1_out), .in2(and_1_out), .in3(or_1_out), .in4(xor_1_out),
    .in5(shifter_1_out), .in6(shifter_2_out), .in7(multiplier_1_out), .out(Output), .sel(\Opération ));
  Multiplexer #(.select(3), .enable("false")) multiplexer_3 (
    .in0(1'b1), .in1(comparator_1_eq), .in2(not_1_out), .in3(comparator_1_gt), .in4(comparator_1_lt),
    .in5(or_2_out), .in6(1'b1), .in7(1'b1), .out(Jump), .sel(\Opération ));
  Comparator #(.width(16)) comparator_1 (
    .a(Input1), .b(Input2), .gt(comparator_1_gt), .eq(comparator_1_eq), .lt(comparator_1_lt));
  not not_1 (not_1_out, comparator_1_eq);
  and and_2 (and_2_out, \Opération [2], \Opération [1]);
  Demultiplexer #(.enable("false")) demultiplexer_1 (.out0(Call), .out1(Return), .in(and_2_out), .sel(\Opération [0]));
  or or_2 (or_2_out, comparator_1_eq, comparator_1_lt);

  // Other names for the same wires on the sheet: Imm_t[15:0] = Input2

  // Notes on the sheet:
  //   Jump
  //   Call
  //   Return
endmodule

module main (
  input  Reset,
  input  ResetRAM
);

  wire and_1_out, and_2_out, and_3_out, and_4_out, Call, Clock, Clock_out, Cond, CTRL, Exec, Fetch,
       getcst_1_imm, Load, not_1_out, ramctrl_1_memload, ramctrl_1_memstore, ramctrl_2_memload,
       ramctrl_2_memstore, Return, Store, WriteReg;
  wire [2:0] GetOp;
  wire [11:0] reg_pcr_1_ppcr;
  wire [15:0] adder_1_out, Addr, addr_store_load, alu_1_output, decodeir_1_jmpaddress, getcst_1_cst,
       JMP_Address, MemIN, PC, R0, R1, R2, R3, R4, R5, R6, R7, registres_1_out_sr1, registres_1_out_sr2;
  wire [31:0] bit_extender_1_out, IR, MemOUT;

  Clock u_Clock (.out(Clock_out));
  Seq seq_1 (.ClockOrig(Clock_out), .reset(Reset), .Fetch(Fetch), .Exec(Exec), .Clock(Clock));
  LED led_1 (.in(Clock_out));
  RegPC regpc_1 (.JMP_Address(JMP_Address), .Cond(Cond), .CTRL(CTRL), .Clock(Exec), .Reset(Reset), .PC(PC));
  // Probe on PC
  GetAddr getaddr_1 (
    .PC(PC), .Addr(Addr), .Fetch(Fetch), .Load(Load), .Store(Store), .addr_store_load(addr_store_load));
  // Probe on Addr
  LED led_2 (.in(Fetch));
  LED led_3 (.in(Exec));
  // Probe on MemIN
  assign bit_extender_1_out = {{16{MemIN[15]}}, MemIN};  // Bit_Extender bit_extender_1
  // Probe on PC
  // Probe on IR
  DecodeIR decodeir_1 (
    .CTRL(CTRL), .WriteReg(WriteReg), .IR(IR), .Load(Load), .JMPAddress(decodeir_1_jmpaddress),
    .Store(Store), .GetOp(GetOp));  // open: IN_OUT
  RamCtrl ramctrl_1 (
    .Store(Store), .Fetch(Fetch), .Exec(Exec), .Load(Load), .MemStore(ramctrl_1_memstore),
    .MemLoad(ramctrl_1_memload), .Clock(Clock));
  // Probe on MemOUT
  RAM #(.addrWidth(16), .dataWidth(32), .bus("separate")) ram_1 (
    .addr(Addr), .din(bit_extender_1_out), .data(MemOUT), .str(ramctrl_1_memstore), .clk(ramctrl_1_memstore),
    .ld(ramctrl_1_memload), .clr(ResetRAM));  // open: sel
  // Probe on R0
  // Probe on R3
  // Probe on R6
  assign JMP_Address = not_1_out ? decodeir_1_jmpaddress : 16'bz;  // Controlled_Buffer controlled_buffer_1
  not not_1 (not_1_out, Return);
  Register #(.width(32), .trigger("falling")) RegIR (.D(MemOUT), .Q(IR), .clk(Fetch), .clr(Reset));  // open: en
  // Probe on R1
  // Probe on R4
  // Probe on R7
  // Probe on IR
  // Probe on R2
  // Probe on R5
  // Probe on IR[8:6]
  // Probe on IR[11:9]
  // Probe on IR[14:12]
  // Probe on getcst_1_cst
  GetCst getcst_1 (.IR(IR), .Cst(getcst_1_cst), .Imm(getcst_1_imm));
  Registres registres_1 (
    .IN(alu_1_output), .WriteReg(WriteReg), .DR(IR[8:6]), .OUT_DR(MemIN), .R0(R0), .R1(R1), .R2(R2), .R3(R3),
    .R4(R4), .R5(R5), .R6(R6), .R7(R7), .Reset(Reset), .Clock(Exec), .STORE(Store), .MemOUT(MemOUT),
    .LOAD(Load), .Addr_STORE_LOAD(addr_store_load), .SR2(IR[14:12]), .SR1(IR[11:9]),
    .OUT_SR2(registres_1_out_sr2), .OUT_SR1(registres_1_out_sr1));
  // Probe on registres_1_out_sr2
  // Probe on registres_1_out_sr1
  ALU alu_1 (
    .Imm(getcst_1_imm), .\Opération (GetOp), .Input2(registres_1_out_sr2), .Input1(registres_1_out_sr1),
    .Cst(getcst_1_cst), .Output(alu_1_output), .Jump(Cond), .Call(Call), .Return(Return));
  // Probe on alu_1_output
  // Probe on R0
  // Probe on R1
  // Probe on R2
  // Probe on R3
  // Probe on R4
  // Probe on R5
  // Probe on R6
  // Probe on R7
  // Probe on alu_1_output
  Reg_PCR reg_pcr_1 (.Call(and_1_out), .Return(and_2_out), .Clock(Fetch), .Reset(Reset), .PPCR(reg_pcr_1_ppcr));
  and and_1 (and_1_out, CTRL, Call);
  and and_2 (and_2_out, CTRL, Return);
  Adder #(.width(16)) adder_1 (.a(16'h1), .b(PC), .out(adder_1_out));  // open: cin, cout
  RamCtrl ramctrl_2 (
    .Store(and_4_out), .Fetch(Fetch), .Exec(Exec), .Load(and_3_out), .MemStore(ramctrl_2_memstore),
    .MemLoad(ramctrl_2_memload), .Clock(Clock));
  RAM #(.addrWidth(12), .dataWidth(16), .bus("separate")) ram_2 (
    .addr(reg_pcr_1_ppcr), .din(adder_1_out), .data(JMP_Address), .str(ramctrl_2_memstore),
    .clk(ramctrl_2_memstore), .ld(ramctrl_2_memload), .clr(Reset));  // open: sel
  and and_3 (and_3_out, CTRL, Return);
  and and_4 (and_4_out, CTRL, Call);

  // Notes on the sheet:
  //   RAM
  //   Pile Call/Return
endmodule

module DecodeIR (
  input  [31:0] IR,
  output WriteReg,
  output Store,
  output Load,
  output IN_OUT,
  output CTRL,
  output [2:0] GetOp,
  output [15:0] JMPAddress
);

  wire comparator_1_gt, comparator_2_eq, decoder_1_out1, or_1_out;
  wire [15:0] multiplexer_1_out;

  Comparator #(.width(3), .mode("unsigned")) comparator_1 (
    .a(IR[4:2]), .b(3'b101), .gt(comparator_1_gt));  // open: eq, lt
  Comparator #(.width(3), .mode("unsigned")) comparator_2 (
    .a(IR[4:2]), .b(3'b000), .eq(comparator_2_eq));  // open: gt, lt
  Decoder #(.select(2), .enable("false")) decoder_1 (
    .out0(WriteReg), .out1(decoder_1_out1), .out2(IN_OUT), .out3(CTRL), .sel(IR[1:0]));
  or or_1 (or_1_out, comparator_2_eq, comparator_1_gt);
  Multiplexer #(.width(16), .enable("false")) multiplexer_1 (
    .in0(IR[27:12]), .in1(IR[21:6]), .out(multiplexer_1_out), .sel(or_1_out));
  assign JMPAddress = CTRL ? multiplexer_1_out : 16'bz;  // Controlled_Buffer controlled_buffer_1
  Demultiplexer #(.enable("false")) demultiplexer_1 (.out0(Store), .out1(Load), .in(decoder_1_out1), .sel(IR[4]));

  assign GetOp = IR[4:2];
endmodule

module GetAddr (
  input  [15:0] PC,
  input  [15:0] addr_store_load,
  input  Load,
  input  Store,
  input  Fetch,
  output [15:0] Addr
);

  wire and_1_out, not_1_out, or_1_out;

  or or_1 (or_1_out, Load, Store);
  not not_1 (not_1_out, Fetch);
  and and_1 (and_1_out, or_1_out, not_1_out);
  Multiplexer #(.width(16), .enable("false")) multiplexer_1 (
    .in0(PC), .in1(addr_store_load), .out(Addr), .sel(and_1_out));
endmodule

module GetCst (
  input  [31:0] IR,
  output [15:0] Cst,
  output Imm
);

  Bit_Extender #(.in_width(20)) bit_extender_1 (.in(IR[31:12]), .out(Cst));
  // Probe on IR[31:12]

  assign Imm = IR[5];
endmodule

module RamCtrl (
  input  Clock,
  input  Exec,
  input  Fetch,
  input  Load,
  input  Store,
  output MemLoad,
  output MemStore
);

  wire and_1_out;

  and and_1 (and_1_out, Exec, Load);
  and and_2 (MemStore, Exec, Clock, Store);
  or or_1 (MemLoad, Fetch, and_1_out);
endmodule

module Registres (
  input  [15:0] IN,
  input  [31:0] MemOUT,
  input  [2:0] SR2,
  input  [2:0] SR1,
  input  [2:0] DR,
  input  WriteReg,
  input  Clock,
  input  Reset,
  input  LOAD,
  input  STORE,
  output [15:0] R0,
  output [15:0] OUT_SR2,
  output [15:0] R1,
  output [15:0] R2,
  output [15:0] R3,
  output [15:0] Addr_STORE_LOAD,
  output [15:0] OUT_SR1,
  output [15:0] R4,
  output [15:0] R5,
  output [15:0] OUT_DR,
  output [15:0] R6,
  output [15:0] R7
);

  wire and_1_out, demultiplexer_1_out0, demultiplexer_1_out1, demultiplexer_1_out2, demultiplexer_1_out3,
       demultiplexer_1_out4, demultiplexer_1_out5, demultiplexer_1_out6, demultiplexer_1_out7, not_1_out,
       or_1_out;
  wire [2:0] SR1_t, SR2_t;
  wire [15:0] demultiplexer_2_out1, multiplexer_1_out, multiplexer_4_out;

  not not_1 (not_1_out, WriteReg);
  // Probe on MemOUT
  or or_1 (or_1_out, WriteReg, LOAD);
  Multiplexer #(.width(16), .enable("false")) multiplexer_1 (
    .in0(IN), .in1(MemOUT[15:0]), .out(multiplexer_1_out), .sel(LOAD));
  Multiplexer #(.width(3), .enable("false")) multiplexer_2 (.in0(SR2), .in1(SR1), .out(SR2_t), .sel(not_1_out));
  Multiplexer #(.width(3), .enable("false")) multiplexer_3 (.in0(SR1), .in1(DR), .out(SR1_t), .sel(not_1_out));
  Demultiplexer #(.select(3), .enable("false")) demultiplexer_1 (
    .out0(demultiplexer_1_out0), .out1(demultiplexer_1_out1), .out2(demultiplexer_1_out2),
    .out3(demultiplexer_1_out3), .out4(demultiplexer_1_out4), .out5(demultiplexer_1_out5),
    .out6(demultiplexer_1_out6), .out7(demultiplexer_1_out7), .in(or_1_out), .sel(DR));
  and and_1 (and_1_out, Clock, STORE);
  Register #(.width(16), .trigger("falling")) u_R0 (
    .D(multiplexer_1_out), .en(demultiplexer_1_out0), .Q(R0), .clk(Clock), .clr(Reset));
  Register #(.width(16), .trigger("falling")) u_R1 (
    .D(multiplexer_1_out), .en(demultiplexer_1_out1), .Q(R1), .clk(Clock), .clr(Reset));
  Register #(.width(16), .trigger("falling")) u_R2 (
    .D(multiplexer_1_out), .en(demultiplexer_1_out2), .Q(R2), .clk(Clock), .clr(Reset));
  Register #(.width(16), .trigger("falling")) u_R3 (
    .D(multiplexer_1_out), .en(demultiplexer_1_out3), .Q(R3), .clk(Clock), .clr(Reset));
  Register #(.width(16), .trigger("falling")) u_R4 (
    .D(multiplexer_1_out), .en(demultiplexer_1_out4), .Q(R4), .clk(Clock), .clr(Reset));
  Register #(.width(16), .trigger("falling")) u_R5 (
    .D(multiplexer_1_out), .en(demultiplexer_1_out5), .Q(R5), .clk(Clock), .clr(Reset));
  Register #(.width(16), .trigger("falling")) u_R6 (
    .D(multiplexer_1_out), .en(demultiplexer_1_out6), .Q(R6), .clk(Clock), .clr(Reset));
  Register #(.width(16), .trigger("falling")) u_R7 (
    .D(multiplexer_1_out), .en(demultiplexer_1_out7), .Q(R7), .clk(Clock), .clr(Reset));
  Multiplexer #(.select(3), .width(16)) multiplexer_4 (
    .in0(R0), .in1(R1), .in2(R2), .in3(R3), .in4(R4), .in5(R5), .in6(R6), .in7(R7), .out(multiplexer_4_out),
    .sel(SR2_t), .en(Clock));
  Multiplexer #(.select(3), .width(16)) multiplexer_5 (
    .in0(R0), .in1(R1), .in2(R2), .in3(R3), .in4(R4), .in5(R5), .in6(R6), .in7(R7), .out(OUT_SR1),
    .sel(SR1_t), .en(Clock));
  Multiplexer #(.select(3), .width(16)) multiplexer_6 (
    .in0(R0), .in1(R1), .in2(R2), .in3(R3), .in4(R4), .in5(R5), .in6(R6), .in7(R7), .out(OUT_DR), .sel(DR),
    .en(Clock));
  Demultiplexer #(.width(16), .enable("false")) demultiplexer_2 (
    .out0(OUT_SR2), .out1(demultiplexer_2_out1), .in(multiplexer_4_out), .sel(and_1_out));
  Multiplexer #(.width(16), .enable("false")) multiplexer_7 (
    .in0(demultiplexer_2_out1), .in1(IN), .out(Addr_STORE_LOAD), .sel(LOAD));

  // Notes on the sheet:
  //   Exec
endmodule

module RegPC (
  input  [15:0] JMP_Address,
  input  CTRL,
  input  Cond,
  input  Clock,
  input  Reset,
  output [15:0] PC
);

  wire and_1_out;
  wire [15:0] adder_1_out, adder_2_out, multiplexer_1_out, multiplexer_2_out, undriven;

  and and_1 (and_1_out, CTRL, Cond);
  Multiplexer #(.width(16), .enable("false")) multiplexer_1 (.out(multiplexer_1_out));  // open: in0, in1, sel
  Adder #(.width(16)) adder_1 (.a(PC), .b(16'h1), .out(adder_1_out));  // open: cin, cout
  Adder #(.width(16)) adder_2 (.a(undriven), .b(multiplexer_1_out), .out(adder_2_out));  // open: cin, cout
  Multiplexer #(.width(16), .enable("false")) multiplexer_2 (
    .in0(adder_1_out), .in1(JMP_Address), .out(multiplexer_2_out), .sel(and_1_out));
  Register #(.width(16), .trigger("falling")) u_PC (
    .D(multiplexer_2_out), .Q(PC), .clk(Clock), .clr(Reset));  // open: en

  // Notes on the sheet:
  //   Jump relatif
endmodule

module Seq (
  input  ClockOrig,
  input  reset,
  output Fetch,
  output Exec,
  output Clock
);

  Register #(.width(1), .trigger("falling")) register_1 (
    .D(Fetch), .Q(Exec), .clk(ClockOrig), .clr(reset));  // open: en
  not not_1 (Fetch, Exec);
  buf buffer_1 (Clock, ClockOrig);
endmodule

module _16_bit_transistor (
  input  [15:0] in_1,
  input  Test,
  output [15:0] Arith
);

  and and_1 (Arith[0], in_1[0], Test);
  and and_2 (Arith[1], in_1[1], Test);
  and and_3 (Arith[2], in_1[2], Test);
  and and_4 (Arith[3], in_1[3], Test);
  and and_5 (Arith[4], in_1[4], Test);
  and and_6 (Arith[5], in_1[5], Test);
  and and_7 (Arith[6], in_1[6], Test);
  and and_8 (Arith[7], in_1[7], Test);
  and and_9 (Arith[8], in_1[8], Test);
  and and_10 (Arith[9], in_1[9], Test);
  and and_11 (Arith[10], in_1[10], Test);
  and and_12 (Arith[11], in_1[11], Test);
  and and_13 (Arith[12], in_1[12], Test);
  and and_14 (Arith[13], in_1[13], Test);
  and and_15 (Arith[14], in_1[14], Test);
  and and_16 (Arith[15], in_1[15], Test);
endmodule

module Reg_PCR (
  input  Call,
  input  Return,
  input  Clock,
  input  Reset,
  output [11:0] PPCR
);

  wire [11:0] adder_1_out, multiplexer_1_out, multiplexer_2_out, PPCR_q, subtractor_1_out, subtractor_2_out;

  Multiplexer #(.width(12), .enable("false")) multiplexer_1 (
    .in0({12{1'b0}}), .in1(12'h1), .out(multiplexer_1_out), .sel(Call));
  Adder #(.width(12)) adder_1 (.a(PPCR_q), .b(multiplexer_1_out), .out(adder_1_out));  // open: cin, cout
  Multiplexer #(.width(12), .enable("false")) multiplexer_2 (
    .in0({12{1'b0}}), .in1(12'h1), .out(multiplexer_2_out), .sel(Return));
  Subtractor #(.width(12)) subtractor_1 (
    .a(adder_1_out), .b(multiplexer_2_out), .out(subtractor_1_out));  // open: bin, bout
  Register #(.width(12)) u_PPCR (.D(subtractor_1_out), .en(1'b1), .Q(PPCR_q), .clk(Clock), .clr(Reset));
  Subtractor #(.width(12)) subtractor_2 (.a(PPCR_q), .b(multiplexer_2_out), .out(subtractor_2_out));  // open: bin, bout
  Multiplexer #(.width(12), .enable("false")) multiplexer_3 (
    .in0(PPCR_q), .in1(subtractor_2_out), .out(PPCR), .sel(Return));

  // Notes on the sheet:
  //   Pointeur Pile Call Return
endmodule
